# Fritzing sketch IEEE_Circuit (saved by Fritzing 1.0.2b)
breadboards: 1

parts:
  Mod1 = Amica NodeMCU DEVKIT 1.0
  HC-SR04_Sensor_1 = HC-SR04 Ultrasonic Distance Sensor
  LED1 = LED - 3mm [color="Red (633nm)" current=0.030A package="3 mm [THT]"]
  LED2 = LED - 3mm [color="Green (555nm)" current=0.030A package="3 mm [THT]"]
  R1 = Resistor [tolerance=±5% resistance=220 package="0402 [SMD]"]
  R2 = Resistor [tolerance=±5% resistance=220 package="0402 [SMD]"]

nets:
  N1: Mod1.pin1, Mod1.pin_10, Mod1.pin_26
  N2: Mod1.pin2, Mod1.pin_9, Mod1.pin_25, Mod1.pin_29, HC-SR04_Sensor_1.GND, LED1.cathode, LED2.cathode
  N3: Mod1.pin5, HC-SR04_Sensor_1.ECHO
  N4: Mod1.pin6, HC-SR04_Sensor_1.TRIG
  N5: Mod1.pin_11, R2.Pin_1
  N6: Mod1.pin_13, R1.Pin_1
  N7: Mod1.pin_30, HC-SR04_Sensor_1.VCC
  N8: LED1.anode, R2.Pin_0
  N9: LED2.anode, R1.Pin_0
